// Logisim project Processador.circ as structural Verilog: 4 circuits, main circuit PROCESSADOR
module PROCESSADOR (
  output [31:0] \INSTRUÇÃO 
);

  wire and_1_out, and_2_out, button_1_out, clock_1_out, not_1_out, or_1_out, or_2_out, uc_1_alusrc, uc_1_bge,
       uc_1_branch, uc_1_jump, uc_1_memread, uc_1_memtoreg, uc_1_memwrite, uc_1_regdst, uc_1_regwrite,
       ula_1_igual, ula_1_maior;
  wire [1:0] uc_1_aluop;
  wire [3:0] multiplexer_1_out;
  wire [31:0] adder_1_out, banco_de_registradores_1_r0_d, banco_de_registradores_1_r1_d, bit_extender_1_out,
       multiplexer_2_out, multiplexer_3_out, multiplexer_4_out, PC_q, ram_1_data, ula_1_ula_out;

  Adder #(.width(32)) adder_1 (.a(PC_q), .b(32'h4), .out(adder_1_out));  // open: cin, cout
  Register #(.width(32)) PC (.D(multiplexer_2_out), .Q(PC_q), .clk(clock_1_out), .clr(button_1_out));  // open: en
  Clock clock_1 (.out(clock_1_out));
  Button button_1 (.out(button_1_out));
  ROM #(.dataWidth(32)) rom_1 (.addr(PC_q[9:2]), .data(\INSTRUÇÃO ));  // open: sel
  uc uc_1 (
    .op1(\INSTRUÇÃO [31]), .op2(\INSTRUÇÃO [30]), .op3(\INSTRUÇÃO [29]), .op4(\INSTRUÇÃO [28]),
    .ALUOP(uc_1_aluop), .branch(uc_1_branch), .jump(uc_1_jump), .regdst(uc_1_regdst),
    .regwrite(uc_1_regwrite), .alusrc(uc_1_alusrc), .memread(uc_1_memread), .memwrite(uc_1_memwrite),
    .memtoreg(uc_1_memtoreg), .BGE(uc_1_bge));
  Multiplexer #(.width(4)) multiplexer_1 (
    .in0(\INSTRUÇÃO [19:16]), .in1(\INSTRUÇÃO [27:24]), .out(multiplexer_1_out), .sel(uc_1_regdst));  // open: en
  BANCO_DE_REGISTRADORES banco_de_registradores_1 (
    .DATA_WRITE(multiplexer_4_out), .R0_D(banco_de_registradores_1_r0_d), .R0(\INSTRUÇÃO [19:16]),
    .R1_D(banco_de_registradores_1_r1_d), .R1(\INSTRUÇÃO [23:20]), .CLK(clock_1_out), .RW(multiplexer_1_out),
    .RESET(button_1_out), .RW_2(uc_1_regwrite));
  Multiplexer #(.width(32)) multiplexer_2 (
    .in0(adder_1_out), .in1(bit_extender_1_out), .out(multiplexer_2_out), .sel(or_1_out));  // open: en
  and and_1 (and_1_out, uc_1_bge, or_2_out);
  ULA ula_1 (
    .DATA_0(banco_de_registradores_1_r0_d), .DATA_1(multiplexer_3_out), .ULA_OUT(ula_1_ula_out),
    .ULA_OP(uc_1_aluop), .IGUAL(ula_1_igual), .ShiftAmount(\INSTRUÇÃO [15:11]), .MAIOR(ula_1_maior));
  Multiplexer #(.width(32)) multiplexer_3 (
    .in0(banco_de_registradores_1_r1_d), .in1(bit_extender_1_out), .out(multiplexer_3_out), .sel(uc_1_alusrc));  // open: en
  or or_1 (or_1_out, and_2_out, and_1_out, uc_1_jump);
  and and_2 (and_2_out, uc_1_branch, ula_1_igual);
  or or_2 (or_2_out, ula_1_igual, ula_1_maior);
  assign bit_extender_1_out = {{24{1'b0}}, \INSTRUÇÃO [10:3]};  // Bit_Extender bit_extender_1
  not not_1 (not_1_out, clock_1_out);
  RAM #(.addrWidth(24), .dataWidth(32), .bus("separate")) ram_1 (
    .addr(ula_1_ula_out[23:0]), .din(banco_de_registradores_1_r1_d), .data(ram_1_data), .str(uc_1_memwrite),
    .clk(not_1_out), .ld(uc_1_memread), .clr(button_1_out));  // open: sel
  Multiplexer #(.width(32)) multiplexer_4 (
    .in0(ula_1_ula_out), .in1(ram_1_data), .out(multiplexer_4_out), .sel(uc_1_memtoreg));  // open: en

  // Notes on the sheet:
  //   OPCODE
  //   RD
  //   RS
  //   RT
  //   SHAMT
  //   ADDR/IMM
  //   contents of rom_1 (hex, n*v repeats v):
  //   e0010 b0c00 c0c00 d0c00 10000 20040 90120250 30000 90320210 44105000 4f302000 144f0000 144c0000
  //   60e40000 330010 80000110 110010 800000b0 10000 20040 90120410 10000 903203d0 44105000 4f302000
  //   144f0000 144d0000 60e40040 330010 800002d0 110010 80000270 10000 20040 90940810 30000 903207d0
  //   44105000 4f302000 144f0000 144b0000 60040080 50a40080 50000 90520790 46105000 4f502000 166f0000
  //   166c0000 50760000 48505000 4f302000 148f0000 188d0000 50980040 39970000 19a90000 60940080 550010
  //   80000590 330010 80000490 110010 80000430
endmodule

module ULA (
  input  [31:0] DATA_0,
  input  [31:0] DATA_1,
  input  [1:0] ULA_OP,
  input  [4:0] ShiftAmount,
  output [31:0] ULA_OUT,
  output MAIOR,
  output IGUAL
);

  wire [31:0] adder_1_out, multiplier_1_out, shifter_1_out, subtractor_1_out;

  Adder #(.width(32)) adder_1 (.a(DATA_0), .b(DATA_1), .out(adder_1_out));  // open: cin, cout
  Subtractor #(.width(32)) subtractor_1 (.a(DATA_0), .b(DATA_1), .out(subtractor_1_out));  // open: bin, bout
  Multiplier #(.width(32)) multiplier_1 (.a(DATA_0), .b(DATA_1), .out(multiplier_1_out));  // open: cin, cout
  Shifter #(.width(32)) shifter_1 (.in(DATA_0), .\dist (ShiftAmount), .out(shifter_1_out));
  Comparator #(.width(32), .mode("unsigned")) comparator_1 (
    .a(DATA_0), .b(DATA_1), .gt(MAIOR), .eq(IGUAL));  // open: lt
  Multiplexer #(.select(2), .width(32), .enable("false")) multiplexer_1 (
    .in0(adder_1_out), .in1(subtractor_1_out), .in2(multiplier_1_out), .in3(shifter_1_out), .out(ULA_OUT),
    .sel(ULA_OP));
endmodule

module BANCO_DE_REGISTRADORES (
  input  [31:0] DATA_WRITE,
  input  [3:0] R0,
  input  [3:0] R1,
  input  CLK,
  input  RESET,
  input  [3:0] RW,
  input  RW_2,
  output [31:0] R0_D,
  output [31:0] R1_D
);

  wire demultiplexer_1_out0, demultiplexer_1_out1, demultiplexer_1_out2, demultiplexer_1_out3,
       demultiplexer_1_out4, demultiplexer_1_out5, demultiplexer_1_out6, demultiplexer_1_out7,
       demultiplexer_1_out8, demultiplexer_1_out9, demultiplexer_1_out10, demultiplexer_1_out11,
       demultiplexer_1_out12, demultiplexer_1_out13, demultiplexer_1_out14, demultiplexer_1_out15;
  wire [31:0] register_1_q, register_2_q, register_3_q, register_4_q, register_5_q, register_6_q,
       register_7_q, register_8_q, register_9_q, register_10_q, register_11_q, register_12_q, register_13_q,
       register_14_q, register_15_q, register_16_q;

  Demultiplexer #(.select(4), .enable("false")) demultiplexer_1 (
    .out0(demultiplexer_1_out0), .out1(demultiplexer_1_out1), .out2(demultiplexer_1_out2),
    .out3(demultiplexer_1_out3), .out4(demultiplexer_1_out4), .out5(demultiplexer_1_out5),
    .out6(demultiplexer_1_out6), .out7(demultiplexer_1_out7), .out8(demultiplexer_1_out8),
    .out9(demultiplexer_1_out9), .out10(demultiplexer_1_out10), .out11(demultiplexer_1_out11),
    .out12(demultiplexer_1_out12), .out13(demultiplexer_1_out13), .out14(demultiplexer_1_out14),
    .out15(demultiplexer_1_out15), .in(RW_2), .sel(RW));
  Register #(.width(32)) register_1 (.en(demultiplexer_1_out0), .Q(register_1_q), .clr(RESET));  // open: D, clk
  Register #(.width(32)) register_2 (
    .D(DATA_WRITE), .en(demultiplexer_1_out1), .Q(register_2_q), .clk(CLK), .clr(RESET));
  Register #(.width(32)) register_3 (
    .D(DATA_WRITE), .en(demultiplexer_1_out2), .Q(register_3_q), .clk(CLK), .clr(RESET));
  Register #(.width(32)) register_4 (
    .D(DATA_WRITE), .en(demultiplexer_1_out3), .Q(register_4_q), .clk(CLK), .clr(RESET));
  Register #(.width(32)) register_5 (
    .D(DATA_WRITE), .en(demultiplexer_1_out4), .Q(register_5_q), .clk(CLK), .clr(RESET));
  Register #(.width(32)) register_6 (
    .D(DATA_WRITE), .en(demultiplexer_1_out5), .Q(register_6_q), .clk(CLK), .clr(RESET));
  Register #(.width(32)) register_7 (
    .D(DATA_WRITE), .en(demultiplexer_1_out6), .Q(register_7_q), .clk(CLK), .clr(RESET));
  Register #(.width(32)) register_8 (
    .D(DATA_WRITE), .en(demultiplexer_1_out7), .Q(register_8_q), .clk(CLK), .clr(RESET));
  Register #(.width(32)) register_9 (
    .D(DATA_WRITE), .en(demultiplexer_1_out8), .Q(register_9_q), .clk(CLK), .clr(RESET));
  Register #(.width(32)) register_10 (
    .D(DATA_WRITE), .en(demultiplexer_1_out9), .Q(register_10_q), .clk(CLK), .clr(RESET));
  Register #(.width(32)) register_11 (
    .D(DATA_WRITE), .en(demultiplexer_1_out10), .Q(register_11_q), .clk(CLK), .clr(RESET));
  Register #(.width(32)) register_12 (
    .D(DATA_WRITE), .en(demultiplexer_1_out11), .Q(register_12_q), .clk(CLK), .clr(RESET));
  Register #(.width(32)) register_13 (
    .D(DATA_WRITE), .en(demultiplexer_1_out12), .Q(register_13_q), .clk(CLK), .clr(RESET));
  Register #(.width(32)) register_14 (
    .D(DATA_WRITE), .en(demultiplexer_1_out13), .Q(register_14_q), .clk(CLK), .clr(RESET));
  Register #(.width(32)) register_15 (
    .D(DATA_WRITE), .en(demultiplexer_1_out14), .Q(register_15_q), .clk(CLK), .clr(RESET));
  Register #(.width(32)) register_16 (
    .D(DATA_WRITE), .en(demultiplexer_1_out15), .Q(register_16_q), .clk(CLK), .clr(RESET));
  Multiplexer #(.select(4), .width(32), .disabled(0), .enable("false")) multiplexer_1 (
    .in0(register_1_q), .in1(register_2_q), .in2(register_3_q), .in3(register_4_q), .in4(register_5_q),
    .in5(register_6_q), .in6(register_7_q), .in7(register_8_q), .in8(register_9_q), .in9(register_10_q),
    .in10(register_11_q), .in11(register_12_q), .in12(register_13_q), .in13(register_14_q),
    .in14(register_15_q), .in15(register_16_q), .out(R0_D), .sel(R0));
  Multiplexer #(.select(4), .width(32), .enable("false")) multiplexer_2 (
    .in0(register_1_q), .in1(register_2_q), .in2(register_3_q), .in3(register_4_q), .in4(register_5_q),
    .in5(register_6_q), .in6(register_7_q), .in7(register_8_q), .in8(register_9_q), .in9(register_10_q),
    .in10(register_11_q), .in11(register_12_q), .in12(register_13_q), .in13(register_14_q),
    .in14(register_15_q), .in15(register_16_q), .out(R1_D), .sel(R1));
endmodule

module uc (
  input  op1,
  input  op2,
  input  op3,
  input  op4,
  output [1:0] ALUOP,
  output branch,
  output jump,
  output regdst,
  output regwrite,
  output alusrc,
  output memread,
  output memwrite,
  output memtoreg,
  output BGE
);

  wire and_1_out, and_2_out, and_3_out, and_4_out, and_5_out, and_6_out, and_9_out, and_10_out, and_11_out,
       and_12_out, and_13_out, and_14_out, not_1_out, not_2_out, not_3_out, not_4_out, not_5_out, not_6_out,
       not_7_out, not_8_out, not_9_out, not_10_out, not_11_out, not_12_out, not_13_out, not_14_out,
       not_15_out, not_16_out, not_17_out, not_18_out, not_19_out, not_20_out, not_21_out, not_22_out,
       not_23_out, not_24_out, not_25_out, not_26_out, not_27_out, not_28_out, not_29_out, not_30_out,
       not_31_out, not_32_out, not_33_out, not_34_out, not_35_out, not_36_out, not_37_out, not_38_out,
       not_39_out, not_40_out, not_41_out, not_42_out;

  not not_1 (not_1_out, op1);
  not not_2 (not_2_out, op2);
  not not_3 (not_3_out, op1);
  not not_4 (not_4_out, op3);
  not not_5 (not_5_out, op4);
  not not_6 (not_6_out, op1);
  not not_7 (not_7_out, op2);
  not not_8 (not_8_out, op4);
  not not_9 (not_9_out, op1);
  not not_10 (not_10_out, op3);
  not not_11 (not_11_out, op4);
  not not_12 (not_12_out, op1);
  not not_13 (not_13_out, op2);
  not not_14 (not_14_out, op3);
  not not_15 (not_15_out, op4);
  not not_16 (not_16_out, op1);
  not not_17 (not_17_out, op2);
  not not_18 (not_18_out, op1);
  not not_19 (not_19_out, op2);
  not not_20 (not_20_out, op1);
  not not_21 (not_21_out, op3);
  not not_22 (not_22_out, op4);
  not not_23 (not_23_out, op1);
  and and_1 (and_1_out, not_23_out, not_24_out);
  not not_24 (not_24_out, op2);
  not not_25 (not_25_out, op1);
  and and_2 (and_2_out, not_25_out, not_26_out);
  not not_26 (not_26_out, op3);
  not not_27 (not_27_out, op1);
  not not_28 (not_28_out, op2);
  not not_29 (not_29_out, op3);
  not not_30 (not_30_out, op4);
  not not_31 (not_31_out, op1);
  not not_32 (not_32_out, op3);
  not not_33 (not_33_out, op1);
  not not_34 (not_34_out, op4);
  not not_35 (not_35_out, op1);
  not not_36 (not_36_out, op3);
  not not_37 (not_37_out, op1);
  not not_38 (not_38_out, op4);
  not not_39 (not_39_out, op1);
  not not_40 (not_40_out, op3);
  not not_41 (not_41_out, op2);
  not not_42 (not_42_out, op3);
  and and_3 (and_3_out, not_1_out, not_2_out, op3, op4);
  or or_1 (ALUOP[0], and_3_out, and_4_out);
  and and_4 (and_4_out, not_3_out, op2, not_4_out, not_5_out);
  and and_5 (and_5_out, not_6_out, not_7_out, op3, not_8_out);
  or or_2 (ALUOP[1], and_5_out, and_6_out);
  and and_6 (and_6_out, not_9_out, op2, not_10_out, not_11_out);
  and and_7 (branch, not_12_out, op2, op3, op4);
  and and_8 (jump, op1, not_13_out, not_14_out, not_15_out);
  and and_9 (and_9_out, not_16_out, not_17_out, op4);
  or or_3 (regdst, and_9_out, and_10_out, and_11_out);
  and and_10 (and_10_out, not_18_out, not_19_out, op3);
  and and_11 (and_11_out, not_20_out, op2, not_21_out, not_22_out);
  or or_4 (regwrite, and_1_out, and_2_out);
  and and_12 (and_12_out, not_27_out, not_28_out, not_29_out, not_30_out);
  and and_13 (and_13_out, not_31_out, op2, not_32_out, op4);
  or or_5 (alusrc, and_12_out, and_13_out, and_14_out);
  and and_14 (and_14_out, not_33_out, op2, op3, not_34_out);
  and and_15 (memread, not_35_out, op2, not_36_out, op4);
  and and_16 (memwrite, not_37_out, op2, op3, not_38_out);
  and and_17 (memtoreg, not_39_out, op2, not_40_out, op4);
  and and_18 (BGE, op1, not_41_out, not_42_out, op4);
endmodule
